# Fritzing sketch big-lantern (saved by Fritzing 0.9.3b)
perfboards: 1

parts:
  BAT1 = Battery Holders [package=battcom_20mm_pth]
  BAT2 = Battery Holders [package=battcom_20mm_pth]
  U1 = attiny85 [package=dip]
  S1 = Reed switch [package=THT]
  LED2 = LEDs [package=led10mm]
  LED3 = LEDs [package=led10mm]
  R1 = Resistor [tolerance=±5% resistance=220 package=THT]

nets:
  N1: BAT1.+, BAT2.+, U1.Pin_8
  N2: BAT2.-, R1.Pin_1
  N3: U1.Pin_4, S1.pin_2
  N4: U1.Pin_5, LED2.C, LED3.A
  N5: U1.Pin_7, S1.pin_1
  N6: LED2.A, LED3.C, R1.Pin_0
