# Fritzing sketch small-lantern (saved by Fritzing 0.9.3b)
perfboards: 1

parts:
  U1 = attiny85 [package=dip]
  S1 = Reed switch [package=THT]
  LED3 = LEDs [package=led10mm]
  R1 = Resistor [tolerance=±5% resistance=220 package=THT]
  BAT2 = Battery Holders [package=battcom_20mm_pth]

nets:
  N1: U1.Pin_4, R1.Pin_0, BAT2.-
  N2: U1.Pin_5, LED3.A
  N3: U1.Pin_7, S1.pin_1
  N4: U1.Pin_8, BAT2.+
  N5: LED3.C, R1.Pin_1
